# Fritzing sketch RC Car Controller (saved by Fritzing 0.9.3b)
breadboards: 1

parts:
  Part1 = Arduino Uno (Rev3)
  Part2 = NRF24L01+ Breakout Board
  Part3 = Thumb Joystick
  R1 = Rotary Potentiometer (Small) [maximum_resistance=100kΩ package=THT]
  C1 = Ceramic Capacitor [capacitance=100nF package="100 mil [THT, multilayer]"]

nets:
  N1: Part1.A0, Part3.HORZ
  N2: Part1.A1, Part3.VERT
  N3: Part1.A2, R1.wiper
  N4: Part1.D8, Part2.CS
  N5: Part1.D9_PWM, Part3.SEL
  N6: Part1.D11_PWM/MOSI, Part2.MOSI
  N7: Part1.D12/MISO, Part2.MISO
  N8: Part1.D13/SCK, Part2.SCK
  N9: Part1.D7, Part2.CE
  3V3: Part1.3V3, Part2.VCC, C1.1
  5V: Part1.5V, Part3.VCC, R1.leg2
  GND: Part1.GND, Part2.GND, Part3.GND, R1.leg1, C1.0

// code stored in the sketch: RC Car Controller.ino
#include <SPI.h>
#include "RF24.h"
RF24 radio(7, 8);
const int PACKETSIZE = 8;
byte packet[PACKETSIZE]; //holds the data
int joySelPin = 9;
int joyXPin = A0;
int joyYPin = A1;
int piezoReadPin = A2;
int radioChannel = 25;//match this with receiver code
byte address[8] = {"30281"};//match this with receiver code
void setup() {
  Serial.begin(9600);
  pinMode(joySelPin, INPUT_PULLUP);
  pinMode(piezoReadPin, INPUT);
  radio.begin();
  radio.setChannel(radioChannel);
  radio.setPALevel(RF24_PA_HIGH);
  radio.stopListening();
  radio.openWritingPipe(address);
}

void loop() {
  // put your main code here, to run repeatedly:
  int *intPacket = (int *) packet;
  intPacket[0] = analogRead(joyXPin);
  intPacket[1] = analogRead(joyYPin);
  intPacket[2] = digitalRead(joySelPin);
  intPacket[3] = analogRead(piezoReadPin);
  radio.write((void*)packet, PACKETSIZE, false);
}
