# Fritzing sketch RC Car (saved by Fritzing 0.9.3b)
breadboards: 1

parts:
  Part1 = Arduino Uno (Rev3)
  IC1 = H-Bridge [package=THT]
  Part2 = NRF24L01+ Breakout Board
  M2 = DC Motor
  M1 = DC Motor
  J1 = Basic Servo
  J2 = Piezo Speaker
  R1 = Resistor [tolerance=±5% resistance=1M package="2010 [SMD]"]
  Yellow_LED = LED - 5mm [color="Yellow (595nm)" package="5 mm [THT]"]
  LED1 = LED - 5mm [color="Red (633nm)" package="5 mm [THT]"]
  LED2 = LED - 5mm [color="Red (633nm)" package="5 mm [THT]"]
  LED3 = Red Laser- 650nm
  S1 = Pushbutton [package="[THT]"]

nets:
  N1: Part1.A0, R1.Pin_1
  N2: Part1.A1, Yellow_LED.anode
  N3: Part1.A2, LED1.anode, LED2.anode
  N4: Part1.A3, LED3.anode
  N5: Part1.A5/SCL, S1.Pin_1
  N6: Part1.D8, Part2.CS
  N7: Part1.D9_PWM, IC1.2A
  N8: Part1.D10_PWM/SS, J1.pulse
  N9: Part1.D11_PWM/MOSI, Part2.MOSI
  N10: Part1.D12/MISO, Part2.MISO
  N11: Part1.D13/SCK, Part2.SCK
  GND: Part1.GND, IC1.GND3, Part2.GND, J1.gnd, J2.pin1, Yellow_LED.cathode, LED3.cathode, S1.Pin_3, S1.Pin_4
  N12: Part1.D2, IC1.3A
  N13: Part1.D3_PWM, IC1.3_4EN
  N14: Part1.D4, IC1.4A
  N15: Part1.D5_PWM, IC1.1A
  N16: Part1.D6_PWM, IC1.1_2EN
  N17: Part1.D7, Part2.CE
  3V3: Part1.3V3, Part2.VCC
  5V: Part1.5V, IC1.VCC1, J1.vcc
  N18: Part1.VIN, IC1.VCC2
  N19: IC1.1Y, M1.pin_1
  N20: IC1.2Y, M1.pin_2
  N21: IC1.3Y, M2.pin_1
  N22: IC1.4Y, M2.pin_2
  N23: J2.pin2, R1.Pin_0
  N24: LED1.cathode, LED2.cathode

custom parts:
  Red Laser- 650nm: A generic laser
